# Fritzing sketch weather (saved by Fritzing 0.9.3b)
circuit board: 9cm x 6cm
breadboards: 1

parts:
  MCU = atmega328 [package=dip]
  10k1 = Resistor [tolerance=±5% resistance=10k package=THT]
  XTAL = Crystal [frequency="16 Mhz" package=THT]
  C3 = Ceramic Capacitor [capacitance=20pF package="100 mil [THT, multilayer]"]
  10k2 = Resistor [tolerance=±5% resistance=10k package=THT]
  SW_light = Pushbutton [package="[THT]"]
  LED8 = male pin header, 3 pins [form="♂ (male)"]
  Power = male pin header, 2 pins [form="♂ (male)"]
  SW_Power = Toggle Switch [package=THT]
  SW_MP3 = Toggle Switch [package=THT]
  MP3 = male pin header, 2 pins [form="♂ (male)"]
  SW_reset = Pushbutton [package="[THT]"]
  C2 = Ceramic Capacitor [capacitance=20pF package="100 mil [THT, multilayer]"]
  C4 = Electrolytic Capacitor [capacitance=1µF package="100 mil [THT, electrolytic]"]
  C1 = Tantalum Capacitor [capacitance=1μF package="100 mil [THT, tantalum]"]
  J2 = female pin header, 5 pins [form="♀ (female)"]
  J3 = female pin header, 3 pins [form="♀ (female)"]
  pms7003 = female pin header, 2 pins [form="♀ (female)"]
  J5 = female pin header, 2 pins [form="♀ (female)"]
  ds1302 = female pin header, 5 pins [form="♀ (female)"]
  LED12 = male pin header, 3 pins [form="♂ (male)"]
  J6 = female pin header, 1 pin [form="♀ (female)"]
  sd = female pin header, 5 pins [form="♀ (female)"]
  J7 = female pin header, 5 pins [form="♀ (female)"]
  J8 = female pin header, 5 pins [form="♀ (female)"]

nets:
  N1: MCU.RESET, 10k1.Pin_1, SW_reset.Pin_3, SW_reset.Pin_4
  N2: MCU.D0_(RX), J2.pin1
  N3: MCU.D1_(TX), J2.pin2
  N4: MCU.D2, J2.pin3, ds1302.pin1
  N5: MCU.D3_(PWM), J2.pin4, ds1302.pin2
  N6: MCU.D4, J2.pin5, sd.pin5
  N7: MCU.VCC, MCU.AVCC, MCU.AREF, 10k1.Pin_0, 10k2.Pin_0, LED8.pin2, SW_Power.L1, SW_MP3.L1, C4.+, C1.+, J5.pin2, ds1302.pin5, LED12.pin2, J6.pin1, J8.pin3, J8.pin4
  N8: MCU.GND, C3.1, SW_light.Pin_1, SW_light.Pin_2, LED8.pin3, Power.pin1, MP3.pin1, SW_reset.Pin_1, SW_reset.Pin_2, C2.1, C4.-, C1.-, J5.pin1, ds1302.pin4, LED12.pin3, sd.pin1, J8.pin2
  N9: MCU.XLAT1, XTAL.pin_0, C2.0
  N10: MCU.XLAT2, XTAL.pin_1, C3.0
  N11: MCU.D5_(PWM), J3.pin1
  N12: MCU.D6_(PWM), J3.pin2, pms7003.pin1
  N13: MCU.D7, J3.pin3, pms7003.pin2
  N14: MCU.D8, 10k2.Pin_1, SW_light.Pin_3, SW_light.Pin_4, ds1302.pin3
  N15: MCU.D9_(PWM), LED8.pin1
  N16: MCU.D11_(PWM), LED12.pin1, sd.pin3
  N17: MCU.D12, sd.pin2
  N18: MCU.D13, sd.pin4, J8.pin5
  N19: MCU.A0, J8.pin1
  N20: MCU.A1, J7.pin5
  N21: MCU.A2, J7.pin4
  N22: MCU.A3, J7.pin3
  N23: MCU.A4, J7.pin2
  N24: MCU.A5, J7.pin1
  N25: Power.pin2, SW_Power.COM
  N26: SW_MP3.COM, MP3.pin2
